# Fritzing sketch BLE_TY51_ADC1015 (saved by Fritzing 0.9.3b)
breadboards: 1

parts:
  R1 = Resistor [tolerance=±5% resistance=10k package=THT]
  R2 = Resistor [tolerance=±5% resistance=10k package=THT]
  LED1 = LED - 5mm [color="Blue (505nm)" package="5 mm [THT]"]
  U1 = mbed_TY51822r3 [package=custrom]
  R3 = Resistor [tolerance=±5% resistance=100 package=THT]
  パーツ1 = Adafruit ADS1015 12Bit I2C ADC [part_number="Adafruit #1083"]
  R4 = Rotary Potentiometer (Small) [maximum_resistance=100kΩ package=THT]
  C1 = Ceramic Capacitor [capacitance=1µF package="200 mil [THT, multilayer]"]

nets:
  VDD: R1.Pin_0, R2.Pin_0, U1.VDD, パーツ1.VDD, R4.leg2
  N1: R1.Pin_1, U1.P0_29_SCL, パーツ1.SCL
  N2: R2.Pin_1, U1.P0_30_SDA, パーツ1.SDA
  N3: LED1.cathode, R3.Pin_0
  N4: LED1.anode, U1.P0_21_LED1
  N5: U1.GND#7, パーツ1.ADDR, パーツ1.GND, R4.leg1, C1.1
  N6: U1.GND#32, R3.Pin_1
  N7: パーツ1.AIN0, R4.wiper, C1.0

custom parts:
  mbed_TY51822r3: BLE module
  Adafruit ADS1015 12Bit I2C ADC: For microcontrollers without an analog-to-digital converter or when you want a higher-precision ADC, the ADS1015 provides 12-bit precision at 3300 samples/second over I2C. The chip can be configured as 4 single-ended input channels, or two differential channels. As a nice bonus, it even includes a programmable gain amplifier, up to x16, to help boost up smaller single/differential signals to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
