# Fritzing sketch BLE_TY51_MultiBlink (saved by Fritzing 0.9.3b)
breadboards: 1

parts:
  LED1 = LED - 5mm [color="Blue (505nm)" package="5 mm [THT]"]
  U1 = mbed_TY51822r3 [package=custrom]
  R3 = Resistor [tolerance=±5% resistance=100 package=THT]
  LED3 = RGB LED (com. cathode, rbg) [package="5 mm [THT]"]
  LED4 = RGB LED (com. cathode, rbg) [package="5 mm [THT]"]
  R4 = Resistor [tolerance=±5% resistance=15 package=THT]

nets:
  N1: LED1.cathode, R3.Pin_0
  N2: LED1.anode, U1.P0_21_LED1
  N3: U1.GND#7, R4.Pin_0
  N4: U1.P0_7, LED3.red_anode
  N5: U1.P0_6, LED3.blue_anode
  N6: U1.P0_5, LED3.green_anode
  N7: U1.P0_4, LED4.red_anode
  N8: U1.P0_3, LED4.blue_anode
  N9: U1.P0_2, LED4.green_anode
  N10: U1.GND#32, R3.Pin_1
  N11: LED3.common_cathode, LED4.common_cathode, R4.Pin_1

custom parts:
  mbed_TY51822r3: BLE module
