# Fritzing sketch BLE_TY51_generic (saved by Fritzing 0.9.3b)
breadboards: 1

parts:
  R1 = Resistor [tolerance=±5% resistance=10k package=THT]
  R2 = Resistor [tolerance=±5% resistance=10k package=THT]
  LED1 = LED - 5mm [color="Blue (505nm)" package="5 mm [THT]"]
  U1 = mbed_TY51822r3 [package=custrom]
  R3 = Resistor [tolerance=±5% resistance=100 package=THT]
  U2 = atmega328 [part_number=arduino package=dip]
  R4 = Resistor [tolerance=±5% resistance=10k package=THT]
  LED2 = LED - 5mm [color="Red (633nm)" package="5 mm [THT]"]
  R5 = Resistor [tolerance=±5% resistance=220 package=THT]
  C1 = Ceramic Capacitor [capacitance=100nF package="100 mil [THT, multilayer]"]

nets:
  VDD: R1.Pin_0, R2.Pin_0, U1.VDD, U2.VCC, U2.AVCC, R4.Pin_0, C1.1
  N1: R1.Pin_1, U1.P0_29_SCL, U2.A5
  N2: R2.Pin_1, U1.P0_30_SDA, U2.A4
  N3: LED1.cathode, R3.Pin_0
  N4: LED1.anode, U1.P0_21_LED1
  GND: U1.GND, R3.Pin_1, U2.GND, R5.Pin_1, C1.0
  N5: U2.RESET, R4.Pin_1
  N6: U2.D13, LED2.anode
  N7: LED2.cathode, R5.Pin_0

custom parts:
  mbed_TY51822r3: BLE module
