# Fritzing sketch BLE_blink (saved by Fritzing 0.9.3b)
breadboards: 1

parts:
  LED1 = LED - 5mm [color="Blue (505nm)" package="5 mm [THT]"]
  U1 = mbed_TY51822r3 [package=custrom]
  R3 = Resistor [tolerance=±5% resistance=100 package=THT]
  R4 = Resistor [tolerance=±5% resistance=330 package=THT]
  LED2 = LED - 5mm [color="Red (633nm)" package="5 mm [THT]"]

nets:
  N1: LED1.cathode, R3.Pin_0
  N2: LED1.anode, U1.P0_21_LED1
  N3: U1.GND#7, R4.Pin_0
  N4: U1.P0_7, LED2.anode
  N5: U1.GND#32, R3.Pin_1
  N6: R4.Pin_1, LED2.cathode

custom parts:
  mbed_TY51822r3: BLE module
