# Fritzing sketch BLE_TY51_Light (saved by Fritzing 0.9.3b)
breadboards: 1

parts:
  R1 = Resistor [tolerance=±5% resistance=10k package=THT]
  R2 = Resistor [tolerance=±5% resistance=10k package=THT]
  LED1 = LED - 5mm [color="Blue (505nm)" package="5 mm [THT]"]
  U1 = mbed_TY51822r3 [package=custrom]
  R3 = Resistor [tolerance=±5% resistance=100 package=THT]
  U2 = Grove Digital Ligiht [part_number="Digital Light Sensor"]

nets:
  VDD: R1.Pin_0, R2.Pin_0, U1.VDD, U2.VDD
  N1: R1.Pin_1, U1.P0_29_SCL, U2.SCL
  N2: R2.Pin_1, U1.P0_30_SDA, U2.SDA
  N3: LED1.cathode, R3.Pin_0
  N4: LED1.anode, U1.P0_21_LED1
  N5: U1.GND#7, U2.GND
  N6: U1.GND#32, R3.Pin_1

custom parts:
  mbed_TY51822r3: BLE module
