# Fritzing sketch BLE_TY51_Servo (saved by Fritzing 0.9.3b)
breadboards: 1

parts:
  R1 = Resistor [tolerance=±5% resistance=10k package=THT]
  R2 = Resistor [tolerance=±5% resistance=10k package=THT]
  LED1 = LED - 5mm [color="Blue (505nm)" package="5 mm [THT]"]
  U1 = mbed_TY51822r3 [package=custrom]
  R3 = Resistor [tolerance=±5% resistance=100 package=THT]
  VCC1 = 4 x AAA Battery Mount
  J1 = Basic Servo
  パーツ1 = 16-Channel 12-bit PWM Servo Driver - I2C [part_number=815]

nets:
  VDD: R1.Pin_0, R2.Pin_0, U1.VDD, パーツ1.VCC
  N1: R1.Pin_1, U1.P0_29_SCL, パーツ1.SCL
  N2: R2.Pin_1, U1.P0_30_SDA, パーツ1.SDA
  N3: LED1.cathode, R3.Pin_0
  N4: LED1.anode, U1.P0_21_LED1
  GND: U1.GND#7, VCC1.-, J1.gnd, パーツ1.GND
  N5: U1.GND#32, R3.Pin_1
  N6: VCC1.+, パーツ1.PWRIN
  N7: J1.vcc, パーツ1.5.0V
  N8: J1.pulse, パーツ1.PWM0

custom parts:
  mbed_TY51822r3: BLE module
  16-Channel 12-bit PWM Servo Driver - I2C: You want to make a cool robot, maybe a hexapod walker, or maybe just a piece of art with a lot of moving parts. Or maybe you want to drive a lot of LEDs with precise PWM output. Using only two pins, control 16 free-running PWM outputs! You can even chain up 62 breakouts to control up to 992 PWM outputs.
