# Fritzing sketch BLE_TY51_sw (saved by Fritzing 0.9.3b)
breadboards: 1

parts:
  LED1 = LED - 5mm [color="Blue (505nm)" package="5 mm [THT]"]
  U1 = mbed_TY51822r3 [package=custrom]
  R3 = Resistor [tolerance=±5% resistance=100 package=THT]
  S1 = Pushbutton [package="[THT]"]

nets:
  N1: LED1.cathode, R3.Pin_0
  N2: LED1.anode, U1.P0_21_LED1
  N3: U1.GND#7, S1.Pin_3, S1.Pin_4
  N4: U1.P0_5, S1.Pin_1, S1.Pin_2
  N5: U1.GND#32, R3.Pin_1

custom parts:
  mbed_TY51822r3: BLE module
